// Logisim project RISC16_Saje.circ as structural Verilog: 8 circuits, main circuit main
module main (
);

  wire button_1_out, clock_1_out, controlunit_1_is_itype, controlunit_1_is_jtype, controlunit_1_reg_write,
       memcontroller_1_load_en, memcontroller_1_store_en;
  wire [1:0] instructiondecoder_1_opcode;
  wire [3:0] instructiondecoder_1_func, instructiondecoder_1_rd, instructiondecoder_1_rs,
       instructiondecoder_1_rt;
  wire [7:0] instructiondecoder_1_imm, memcontroller_1_data;
  wire [15:0] alu_1_result, bit_extender_1_out, instructiondecoder_1_jump_addr, multiplexer_1_out,
       multiplexer_2_out, pc_1_o, registerfile_1_rs_out, registerfile_1_rt_out;
  wire [17:0] rom_1_data;

  Clock clock_1 (.out(clock_1_out));
  Button button_1 (.out(button_1_out));
  Multiplexer #(.enable("true"), .width(16)) multiplexer_1 (
    .in1(instructiondecoder_1_jump_addr), .out(multiplexer_1_out), .sel(controlunit_1_is_jtype),
    .en(controlunit_1_is_jtype));  // open: in0
  PC pc_1 (
    .JMP_ADDR(multiplexer_1_out), .JMP_EN(controlunit_1_is_jtype), .EN(clock_1_out), .CLK(clock_1_out),
    .O(pc_1_o));
  ROM #(.addrWidth(16), .dataWidth(18)) rom_1 (.addr(pc_1_o), .data(rom_1_data));
  InstructionDecoder instructiondecoder_1 (
    .isImm(controlunit_1_is_itype), .in_2(rom_1_data), .opcode(instructiondecoder_1_opcode),
    .RD(instructiondecoder_1_rd), .RS(instructiondecoder_1_rs), .RT(instructiondecoder_1_rt),
    .Func(instructiondecoder_1_func), .Imm(instructiondecoder_1_imm),
    .jump_addr(instructiondecoder_1_jump_addr));
  assign bit_extender_1_out = {{8{1'b0}}, instructiondecoder_1_imm};  // Bit_Extender bit_extender_1
  Multiplexer #(.width(16)) multiplexer_2 (
    .in0(alu_1_result), .in1(bit_extender_1_out), .out(multiplexer_2_out), .sel(controlunit_1_is_itype));
  ControlUnit controlunit_1 (
    .opcode_in(instructiondecoder_1_opcode), .reg_write(controlunit_1_reg_write),
    .is_Itype(controlunit_1_is_itype), .is_Jtype(controlunit_1_is_jtype));
  RegisterFile registerfile_1 (
    .write_data(multiplexer_2_out), .rs(instructiondecoder_1_rs), .rt(instructiondecoder_1_rt),
    .rd(instructiondecoder_1_rd), .write_en(controlunit_1_reg_write), .clk(clock_1_out), .rst(button_1_out),
    .rs_out(registerfile_1_rs_out), .rt_out(registerfile_1_rt_out));
  ALU alu_1 (
    .Input1(registerfile_1_rs_out), .Input2(registerfile_1_rt_out), .sel_func(instructiondecoder_1_func),
    .result(alu_1_result));
  MemController memcontroller_1 (
    .func(instructiondecoder_1_func), .en(controlunit_1_is_itype), .write_data(instructiondecoder_1_imm),
    .store_en(memcontroller_1_store_en), .load_en(memcontroller_1_load_en), .data(memcontroller_1_data));
  RAM ram_1 (
    .addr(memcontroller_1_data), .we(memcontroller_1_store_en), .oe(memcontroller_1_load_en),
    .clk(clock_1_out));  // open: din, dout

  // Notes on the sheet:
  //   Global Clock
  //   Global Reset
  //   CLK Signal
  //   RST Signal
  //   is_jtype_signal
  //   contents of rom_1 (hex, n*v repeats v):
  //   10101 10202 312 30001
  //   Instr[15:0] - Jump Address
  //   Decode Instruction
  //   Instr[1:0]
  //   extendedImm[15:0]
  //   Imm or ALU Value
  //   aluResult[15:0]
endmodule

module OneTickLatch (
  input  CLK,
  output out_2
);

  wire not_1_out, register_1_q;

  Register #(.width(1)) register_1 (.D(1'b1), .clk(CLK), .Q(register_1_q));  // open: en, clr
  not not_1 (not_1_out, register_1_q);
  and and_1 (out_2, not_1_out, CLK);
endmodule

module PC (
  input  [15:0] JMP_ADDR,
  input  JMP_EN,
  input  EN,
  input  CLK,
  output [15:0] O
);

  wire oneticklatch_1_out_2;
  wire [15:0] adder_1_out, multiplexer_1_out;

  Adder #(.width(16)) adder_1 (.a(O), .b(16'h1), .out(adder_1_out));  // open: cin, cout
  Register #(.width(16)) register_1 (.D(multiplexer_1_out), .en(EN), .clk(CLK), .Q(O), .clr(oneticklatch_1_out_2));
  Multiplexer #(.width(16)) multiplexer_1 (.in0(adder_1_out), .in1(JMP_ADDR), .out(multiplexer_1_out), .sel(JMP_EN));
  OneTickLatch oneticklatch_1 (.CLK(CLK), .out_2(oneticklatch_1_out_2));
endmodule

module ALU (
  input  [15:0] Input1,
  input  [15:0] Input2,
  input  [3:0] sel_func,
  output [15:0] result
);

  wire [15:0] adder_1_out, and_1_out, divider_1_out, multiplier_1_out, nand_1_out, nor_1_out, or_1_out,
       subtractor_1_out, xor_1_out;

  Adder #(.width(16)) adder_1 (.a(Input1), .b(Input2), .out(adder_1_out));  // open: cin, cout
  Subtractor #(.width(16)) subtractor_1 (.a(Input1), .b(Input2), .out(subtractor_1_out));  // open: bin, bout
  Multiplier #(.width(16)) multiplier_1 (.a(Input1), .b(Input2), .out(multiplier_1_out));  // open: cin, cout
  Divider #(.width(16)) divider_1 (.a(Input1), .b(Input2), .out(divider_1_out));  // open: upper, rem
  assign and_1_out = Input1 & Input2;  // AND_Gate and_1, 16 bits wide
  assign or_1_out = Input1 | Input2;  // OR_Gate or_1, 16 bits wide
  assign xor_1_out = Input1 ^ Input2;  // XOR_Gate xor_1, 16 bits wide
  assign nand_1_out = ~(Input1 & Input2);  // NAND_Gate nand_1, 16 bits wide
  assign nor_1_out = ~(Input1 | Input2);  // NOR_Gate nor_1, 16 bits wide
  Multiplexer #(.select(4), .width(16)) multiplexer_1 (
    .in0(adder_1_out), .in1(subtractor_1_out), .in2(multiplier_1_out), .in3(divider_1_out), .in4(and_1_out),
    .in5(or_1_out), .in6(xor_1_out), .in7(nand_1_out), .in8(nor_1_out), .out(result), .sel(sel_func));  // open: in9, in10, in11, in12, in13, in14, in15
endmodule

module RegisterFile (
  input  [15:0] write_data,
  input  [3:0] rs,
  input  [3:0] rt,
  input  [3:0] rd,
  input  write_en,
  input  clk,
  input  rst,
  output [15:0] rs_out,
  output [15:0] rt_out
);

  wire and_1_out, and_2_out, and_3_out, and_4_out, and_5_out, and_6_out, and_7_out, and_8_out, and_9_out,
       and_10_out, and_11_out, and_12_out, and_13_out, and_14_out, and_15_out, and_16_out, decoder_1_out0,
       decoder_1_out1, decoder_1_out2, decoder_1_out3, decoder_1_out4, decoder_1_out5, decoder_1_out6,
       decoder_1_out7, decoder_1_out8, decoder_1_out9, decoder_1_out10, decoder_1_out11, decoder_1_out12,
       decoder_1_out13, decoder_1_out14, decoder_1_out15, oneticklatch_1_out_2, or_1_out;
  wire [15:0] Reg0_q, Reg1_q, Reg2_q, Reg3_q, Reg4_q, Reg5_q, Reg6_q, Reg7_q, Reg8_q, Reg9_q, Reg10_q,
       Reg11_q, Reg12_q, Reg13_q, Reg14_q, Reg15_q;

  Decoder #(.select(4)) decoder_1 (
    .out0(decoder_1_out0), .out1(decoder_1_out1), .out2(decoder_1_out2), .out3(decoder_1_out3),
    .out4(decoder_1_out4), .out5(decoder_1_out5), .out6(decoder_1_out6), .out7(decoder_1_out7),
    .out8(decoder_1_out8), .out9(decoder_1_out9), .out10(decoder_1_out10), .out11(decoder_1_out11),
    .out12(decoder_1_out12), .out13(decoder_1_out13), .out14(decoder_1_out14), .out15(decoder_1_out15),
    .sel(rd));  // open: en
  and and_1 (and_1_out, decoder_1_out0, write_en);
  and and_2 (and_2_out, decoder_1_out2, write_en);
  and and_3 (and_3_out, decoder_1_out4, write_en);
  and and_4 (and_4_out, decoder_1_out6, write_en);
  and and_5 (and_5_out, decoder_1_out8, write_en);
  and and_6 (and_6_out, decoder_1_out10, write_en);
  and and_7 (and_7_out, decoder_1_out12, write_en);
  and and_8 (and_8_out, decoder_1_out14, write_en);
  Register #(.width(16)) Reg0 (.D({16{1'b0}}), .en(and_1_out), .clk(clk), .Q(Reg0_q), .clr(rst));
  Register #(.width(16)) Reg2 (.D(write_data), .en(and_2_out), .clk(clk), .Q(Reg2_q), .clr(rst));
  Register #(.width(16)) Reg4 (.D(write_data), .en(and_3_out), .clk(clk), .Q(Reg4_q), .clr(rst));
  Register #(.width(16)) Reg6 (.D(write_data), .en(and_4_out), .clk(clk), .Q(Reg6_q), .clr(rst));
  Register #(.width(16)) Reg8 (.D(write_data), .en(and_5_out), .clk(clk), .Q(Reg8_q), .clr(rst));
  Register #(.width(16)) Reg10 (.D(write_data), .en(and_6_out), .clk(clk), .Q(Reg10_q), .clr(rst));
  Register #(.width(16)) Reg12 (.D(write_data), .en(and_7_out), .clk(clk), .Q(Reg12_q), .clr(rst));
  Register #(.width(16)) Reg14 (.D(write_data), .en(and_8_out), .clk(clk), .Q(Reg14_q), .clr(rst));
  OneTickLatch oneticklatch_1 (.CLK(clk), .out_2(oneticklatch_1_out_2));
  or or_1 (or_1_out, rst, oneticklatch_1_out_2);
  Register #(.width(16)) Reg1 (.D(write_data), .en(and_9_out), .clk(clk), .Q(Reg1_q), .clr(or_1_out));
  and and_9 (and_9_out, decoder_1_out1, write_en);
  Register #(.width(16)) Reg3 (.D(write_data), .en(and_10_out), .clk(clk), .Q(Reg3_q), .clr(or_1_out));
  and and_10 (and_10_out, decoder_1_out3, write_en);
  Register #(.width(16)) Reg5 (.D(write_data), .en(and_11_out), .clk(clk), .Q(Reg5_q), .clr(or_1_out));
  and and_11 (and_11_out, decoder_1_out5, write_en);
  Register #(.width(16)) Reg7 (.D(write_data), .en(and_12_out), .clk(clk), .Q(Reg7_q), .clr(or_1_out));
  and and_12 (and_12_out, decoder_1_out7, write_en);
  Register #(.width(16)) Reg9 (.D(write_data), .en(and_13_out), .clk(clk), .Q(Reg9_q), .clr(or_1_out));
  and and_13 (and_13_out, decoder_1_out9, write_en);
  Register #(.width(16)) Reg11 (.D(write_data), .en(and_14_out), .clk(clk), .Q(Reg11_q), .clr(or_1_out));
  and and_14 (and_14_out, decoder_1_out11, write_en);
  Register #(.width(16)) Reg13 (.D(write_data), .en(and_15_out), .clk(clk), .Q(Reg13_q), .clr(or_1_out));
  and and_15 (and_15_out, decoder_1_out13, write_en);
  Register #(.width(16)) Reg15 (.D(write_data), .en(and_16_out), .clk(clk), .Q(Reg15_q), .clr(or_1_out));
  and and_16 (and_16_out, decoder_1_out15, write_en);
  Multiplexer #(.select(4), .width(16)) multiplexer_1 (
    .in0(Reg0_q), .in1(Reg1_q), .in2(Reg2_q), .in3(Reg3_q), .in4(Reg4_q), .in5(Reg5_q), .in6(Reg6_q),
    .in7(Reg7_q), .in8(Reg8_q), .in9(Reg9_q), .in10(Reg10_q), .in11(Reg11_q), .in12(Reg12_q), .in13(Reg13_q),
    .in14(Reg14_q), .in15(Reg15_q), .out(rs_out), .sel(rs));
  Multiplexer #(.select(4), .width(16)) multiplexer_2 (
    .in0(Reg0_q), .in1(Reg1_q), .in2(Reg2_q), .in3(Reg3_q), .in4(Reg4_q), .in5(Reg5_q), .in6(Reg6_q),
    .in7(Reg7_q), .in8(Reg8_q), .in9(Reg9_q), .in10(Reg10_q), .in11(Reg11_q), .in12(Reg12_q), .in13(Reg13_q),
    .in14(Reg14_q), .in15(Reg15_q), .out(rt_out), .sel(rt));
endmodule

module ControlUnit (
  input  [1:0] opcode_in,
  output reg_write,
  output is_Itype,
  output is_Jtype
);

  wire multiplexer_1_out;

  Multiplexer #(.select(2)) multiplexer_1 (
    .in0(1'b1), .in1(1'b0), .in2(1'b0), .in3(1'b0), .out(multiplexer_1_out), .sel(opcode_in));
  Multiplexer #(.select(2)) multiplexer_2 (
    .in0(1'b0), .in1(1'b1), .in2(1'b0), .in3(1'b0), .out(is_Itype), .sel(opcode_in));
  Multiplexer #(.select(2)) multiplexer_3 (
    .in0(1'b0), .in1(1'b0), .in2(1'b0), .in3(1'b1), .out(is_Jtype), .sel(opcode_in));
  or or_1 (reg_write, multiplexer_1_out, is_Itype);
endmodule

module MemController (
  input  [3:0] func,
  input  en,
  input  [7:0] write_data,
  output store_en,
  output load_en,
  output [7:0] data
);

  Multiplexer #(.enable("true"), .select(2)) multiplexer_1 (
    .in0(1'b1), .in1(1'b0), .in2(1'b0), .in3(1'b0), .out(store_en), .sel(func[1:0]), .en(en));
  Multiplexer #(.enable("true"), .select(2)) multiplexer_2 (
    .in0(1'b0), .in1(1'b1), .in2(1'b0), .in3(1'b0), .out(load_en), .sel(func[1:0]), .en(en));

  assign data = write_data;
endmodule

module InstructionDecoder (
  input  isImm,
  input  [17:0] in_2,
  output [1:0] opcode,
  output [3:0] RD,
  output [3:0] RS,
  output [3:0] RT,
  output [3:0] Func,
  output [7:0] Imm,
  output [15:0] jump_addr
);

  wire not_1_out;

  not not_1 (not_1_out, isImm);
  Multiplexer #(.width(4)) multiplexer_1 (.in0(in_2[7:4]), .in1(in_2[11:8]), .out(RS), .sel(not_1_out));

  assign Func = in_2[15:12];
  assign Imm = in_2[7:0];
  assign jump_addr = in_2[15:0];
  assign opcode = in_2[17:16];
  assign RD = in_2[7:4];
  assign RT = in_2[3:0];

  // Notes on the sheet:
  //   Decode Instruction
  //   Instr[15:12] - Func
  //   Instr[7:0] - Immediate Value
  //   Instr[7:4]
endmodule
